# Fritzing sketch photon_demo_hardware (saved by Fritzing 0.9.2b)
circuit board: 3.79872cm x 2.12795cm
breadboards: 1

parts:
  Part1 = Photon
  R2 = PHOTOCELL [package=photocell]
  POT1 = Breadboard Trimpot

nets:
  N1: Part1.A0, R2.P$2, POT1.PIN3
  N2: Part1.GND, POT1.PIN2
  N3: Part1.3V3, R2.P$1
